# Fritzing sketch Unipolar_buttons (saved by Fritzing 0.9.3b)
breadboards: 1

parts:
  SM1 = 28BYJ-48 Stepper Motor [part_number=28BYJ-48]
  Part1 = Arduino Uno (Rev3)
  S2 = Pushbutton [package="[THT]"]
  S3 = Pushbutton [package="[THT]"]
  Driver1 = 28BYJ-48 Driver Module [part_number=ULN2003 package=THT]
  C6 = Electrolytic Capacitor [capacitance=100µF package="200 mil [THT, electrolytic]"]
  Power_plug1 = Power plug

nets:
  N1: SM1.blue-pin, Driver1.blue-pin
  N2: SM1.pink-pin, Driver1.pink-pin
  N3: SM1.yellow-pin, Driver1.yellow-pin
  N4: SM1.orange-pin, Driver1.orange-pin
  N5: SM1.red-pin, Driver1.red-pin
  N6: Part1.D8, Driver1.IN1
  N7: Part1.D9_PWM, Driver1.IN2
  N8: Part1.D10_PWM/SS, Driver1.IN3
  N9: Part1.D11_PWM/MOSI, Driver1.IN4
  N10: Part1.D2, S2.Pin_1, S2.Pin_2
  N11: Part1.D3_PWM, S3.Pin_1, S3.Pin_2
  5V: Part1.5V, Driver1.Vmotor, C6.+, Power_plug1.VCC
  GND: Part1.GND, S2.Pin_3, S2.Pin_4, S3.Pin_3, S3.Pin_4, Driver1.GND, C6.-, Power_plug1.GND

custom parts:
  28BYJ-48 Stepper Motor: Unipolar Stepper Motor 28BYJ-48 Top coil - pink & orange Bottom coil - blue & yellow Common rail - red Connector pins: blue - pink - yellow - orange - red
  28BYJ-48 Driver Module: ULN2003 Driver Module for the 28BYJ-48 Unipolar Stepper Motor LED A - Blue wire - Bottom coil left LED B - Pink wire - Top coil left LED C - Yellow wire - Bottom coil right LED D - Orange wire - Top coil right Common rail - red Connector pins: blue - pink - yellow - orange - red Control pins - IN1 to IN4 Power pins - GND & Vmotor (5-12V) On/Off jumper (if removed, power to motor is cut).
